# Fritzing sketch circuit (saved by Fritzing 1.0.3b)
stripboards: 3

parts:
  Part1 = Adafruit BMP280 [part_number="Adafruit #2651"]
  Mod1 = Raspberry Pi 4B
  F1 = Fan - Ventilador [package=THT]
  R1 = Resistor [tolerance=±5% resistance=220 package="2512 [SMD]"]
  Q1 = NPN-Transistor [package="TO92 [THT]"]
  J1 = Screw terminal - 2 pins [package=THT]
  J2 = Screw terminal - 2 pins [package=THT]
  J3 = Screw terminal - 2 pins [package=THT]
  J4 = Screw terminal - 2 pins [package=THT]
  Gravity_Digital_Microwave_Sensor1 = Gravity: Digital Microwave Sensor [package=sot23-3]
  M1 = RioRand LM2596
  USB_C_Plug1 = USB C Plug [package=micro-b-ra-th]
  12V_LED_Array1 = 12V LED Array
  R2 = Resistor [tolerance=±5% resistance=220 package="2512 [SMD]"]
  Q2 = NPN-Transistor [package="TO92 [THT]"]
  J5 = Power Jack [package=power_jack_combo]

nets:
  VCC: Part1.VCC, Mod1.3V3
  N1: Part1.GND, Mod1.GPIO4
  N2: Part1.SCK/SCL, Mod1.GPIO3
  N3: Part1.SDI/SDA, Mod1.GPIO2
  5V: Mod1.5V, Gravity_Digital_Microwave_Sensor1.VCC
  GND: Mod1.GND, Gravity_Digital_Microwave_Sensor1.GND
  N4: Mod1.GPIO27, Gravity_Digital_Microwave_Sensor1.SDO
  N5: Mod1.GPIO22, R1.Pin_0, R1.Pin_1, Q1.C
  N6: Mod1.GPIO23, R2.Pin_0, R2.Pin_1, Q2.C
  5V_2: F1.5V, J1.pin2, J2.pin2, J3.pin2, J4.pin2, M1.Pin_1, 12V_LED_Array1.VCC, J5.PWR
  N7: F1.GND, Q1.E
  N8: Q1.B, J1.pin1, J2.pin1, J3.pin1, J4.pin1, M1.Pin_2, Q2.B, J5.GND
  N9: M1.Pin_3, USB_C_Plug1.VCC
  N10: M1.Pin_4, USB_C_Plug1.GND
  N11: 12V_LED_Array1.GND, Q2.E

notes:
  Track should be broken between resistor connections

custom parts:
  Adafruit BMP280: Bosch has stepped up their game with their new BMP280 sensor, an environmental sensor with temperature, barometric pressure that is the next generation upgrade to the BMP085/BMP180/BMP183. This sensor is great for all sorts of weather sensing and can even be used in both I2C and SPI! This precision sensor from Bosch is the best low-cost, precision sensing solution for measuring barometric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
  Fan - Ventilador: Ventilador de 2 pines, se encuentra comunmente en computadoras de escritorio
